# Fritzing sketch whackamole (saved by Fritzing 0.9.4)
breadboards: 1

parts:
  S1 = Pushbutton [package="[THT]"]
  S2 = Pushbutton [package="[THT]"]
  S3 = Pushbutton [package="[THT]"]
  LED1 = LED - 5mm [color="Red (633nm)" package="5 mm [THT]"]
  LED2 = LED - 5mm [color="Red (633nm)" package="5 mm [THT]"]
  LED3 = LED - 5mm [color="Red (633nm)" package="5 mm [THT]"]
  R1 = Resistor [tolerance=±5% resistance=220 package=THT]
  R2 = Resistor [tolerance=±5% resistance=220 package=THT]
  R3 = Resistor [tolerance=±5% resistance=220 package=THT]
  LED4 = LED - 5mm [color="Green (555nm)" package="5 mm [THT]"]
  J1 = Piezo Speaker
  Part1 = Arduino BT

nets:
  N1: S1.Pin_1, S1.Pin_2, S2.Pin_3, S2.Pin_4, S3.Pin_1, S3.Pin_2, R2.Pin_0, R3.Pin_0, Part1.D2, Part1.PWM_D3, Part1.3V3
  N2: S1.Pin_3, S1.Pin_4
  N3: S2.Pin_1, S2.Pin_2, R1.Pin_0, Part1.D8
  N4: S3.Pin_3, S3.Pin_4
  N5: LED1.cathode, LED2.cathode, LED3.cathode, R1.Pin_1, R2.Pin_1, R3.Pin_1, LED4.cathode, Part1.GND
  N6: LED1.anode, Part1.MOSI/PWM_D11
  N7: LED2.anode, Part1.MISO/D12
  N8: LED3.anode, Part1.SCK/D13
  N9: LED4.anode, Part1.RESET_WT11/D7
  N10: J1.pin2, Part1.PWM_D6
